// Logisim project Traffic_light_gen1.circ as structural Verilog: 5 circuits, main circuit counter_to_7segDisplay
module main (
);

  wire and_1_out, and_2_out, button_1_out, button_2_out, clock_1_out, counter_to_7segdisplay_1_a,
       counter_to_7segdisplay_1_b, counter_to_7segdisplay_1_c, counter_to_7segdisplay_1_d,
       counter_to_7segdisplay_1_e, counter_to_7segdisplay_1_f, counter_to_7segdisplay_1_g,
       counter_to_7segdisplay_2_a, counter_to_7segdisplay_2_b, counter_to_7segdisplay_2_c,
       counter_to_7segdisplay_2_d, counter_to_7segdisplay_2_e, counter_to_7segdisplay_2_f,
       counter_to_7segdisplay_2_g, j_k_ff_1_q, j_k_ff_2_q, j_k_ff_3_q, j_k_ff_4_q, j_k_ff_5_q,
       n4bitcounte__to_led_1_u1, n4bitcounte__to_led_1_u2, n4bitcounte__to_led_1_u3, not_1_out, not_2_out,
       not_3_out, not_4_out, or_1_out, pedestrian_contr_1_g, pedestrian_contr_1_r, xor_1_out;

  Clock clock_1 (.out(clock_1_out));
  Button button_1 (.out(button_1_out));
  and and_1 (and_1_out, clock_1_out, j_k_ff_1_q);
  and and_2 (and_2_out, clock_1_out, not_1_out);
  not not_1 (not_1_out, j_k_ff_1_q);
  J_K_Flip_Flop j_k_ff_1 (.J(1'b1), .clk(button_1_out), .K(1'b1), .Q(j_k_ff_1_q));  // open: Qn, preset, en, reset
  J_K_Flip_Flop j_k_ff_2 (
    .J(1'b1), .clk(and_1_out), .K(1'b1), .Q(j_k_ff_2_q), .reset(or_1_out));  // open: Qn, preset, en
  or or_1 (or_1_out, button_1_out, button_2_out);
  counter_to_7segDisplay counter_to_7segdisplay_1 (
    .a1(1'b1), .a2(1'b0), .a3(1'b1), .a4(1'b0), .e(counter_to_7segdisplay_1_e),
    .d(counter_to_7segdisplay_1_d), .c(counter_to_7segdisplay_1_c), .b(counter_to_7segdisplay_1_b),
    .a(counter_to_7segdisplay_1_a), .f(counter_to_7segdisplay_1_f), .g(counter_to_7segdisplay_1_g));
  not not_2 (not_2_out, j_k_ff_2_q);
  _7_Segment_Display u_7_segment_display_1 (
    .g(counter_to_7segdisplay_1_g), .f(counter_to_7segdisplay_1_f), .a(counter_to_7segdisplay_1_a),
    .b(counter_to_7segdisplay_1_b), .e(counter_to_7segdisplay_1_e), .d(counter_to_7segdisplay_1_d),
    .c(counter_to_7segdisplay_1_c));  // open: dp
  J_K_Flip_Flop j_k_ff_3 (
    .J(1'b1), .clk(not_2_out), .K(1'b1), .Q(j_k_ff_3_q), .preset(button_2_out), .reset(button_1_out));  // open: Qn, en
  not not_3 (not_3_out, j_k_ff_3_q);
  J_K_Flip_Flop j_k_ff_4 (
    .J(1'b1), .clk(not_3_out), .K(1'b1), .Q(j_k_ff_4_q), .preset(button_2_out), .reset(button_1_out));  // open: Qn, en
  not not_4 (not_4_out, j_k_ff_4_q);
  J_K_Flip_Flop j_k_ff_5 (
    .J(1'b1), .clk(not_4_out), .K(1'b1), .Q(j_k_ff_5_q), .preset(button_1_out), .reset(button_2_out));  // open: Qn, en
  counter_to_7segDisplay counter_to_7segdisplay_2 (
    .a1(j_k_ff_5_q), .a2(j_k_ff_4_q), .a3(j_k_ff_3_q), .a4(j_k_ff_2_q), .e(counter_to_7segdisplay_2_e),
    .d(counter_to_7segdisplay_2_d), .c(counter_to_7segdisplay_2_c), .b(counter_to_7segdisplay_2_b),
    .a(counter_to_7segdisplay_2_a), .f(counter_to_7segdisplay_2_f), .g(counter_to_7segdisplay_2_g));
  _7_Segment_Display u_7_segment_display_2 (
    .g(counter_to_7segdisplay_2_g), .f(counter_to_7segdisplay_2_f), .a(counter_to_7segdisplay_2_a),
    .b(counter_to_7segdisplay_2_b), .e(counter_to_7segdisplay_2_e), .d(counter_to_7segdisplay_2_d),
    .c(counter_to_7segdisplay_2_c));  // open: dp
  _4bitcounte__to_led u_4bitcounte__to_led_1 (
    .a1(j_k_ff_5_q), .a2(j_k_ff_4_q), .a3(j_k_ff_3_q), .a4(j_k_ff_2_q), .u1(n4bitcounte__to_led_1_u1),
    .u2(n4bitcounte__to_led_1_u2), .u3(n4bitcounte__to_led_1_u3));
  pedestrian_contr pedestrian_contr_1 (
    .a1(j_k_ff_5_q), .a2(j_k_ff_4_q), .a3(j_k_ff_3_q), .a4(j_k_ff_2_q), .g(pedestrian_contr_1_g),
    .r(pedestrian_contr_1_r));
  Button button_2 (.out(button_2_out));
  LED led_1 (.in(pedestrian_contr_1_r));
  LED led_2 (.in(n4bitcounte__to_led_1_u1));
  LED led_3 (.in(xor_1_out));
  xor xor_1 (xor_1_out, and_2_out, n4bitcounte__to_led_1_u2);
  LED led_4 (.in(n4bitcounte__to_led_1_u3));
  LED led_5 (.in(pedestrian_contr_1_g));

  // Notes on the sheet:
  //   SERVICE BUTTON
  //   PEDSTRIAN BUTON
endmodule

module Counter_to_light (
  input  a1,
  input  a2,
  input  a3,
  output u1,
  output u2,
  output u3
);

  wire and_1_out, and_2_out, not_1_out, not_2_out;

  and and_1 (and_1_out, a1, a3);
  and and_2 (and_2_out, a1, a2);
  not not_1 (not_1_out, a2);
  not not_2 (not_2_out, a3);
  not not_3 (u3, a1);
  or or_1 (u1, and_1_out, and_2_out);
  and and_3 (u2, a1, not_1_out, not_2_out);
endmodule

module _4bitcounte__to_led (
  input  a1,
  input  a2,
  input  a3,
  input  a4,
  output u1,
  output u2,
  output u3
);

  wire and_1_out, and_2_out, and_3_out, and_4_out, and_5_out, and_6_out, and_7_out, not_1_out, not_2_out,
       not_3_out, not_4_out, not_5_out, not_6_out, not_7_out, not_8_out;

  and and_1 (and_1_out, a1, a4);
  and and_2 (and_2_out, a1, a3);
  and and_3 (and_3_out, a1, a2);
  not not_1 (not_1_out, a1);
  not not_2 (not_2_out, a2);
  not not_3 (not_3_out, a3);
  not not_4 (not_4_out, a4);
  not not_5 (not_5_out, a1);
  and and_4 (and_4_out, not_5_out, not_6_out);
  not not_6 (not_6_out, a2);
  not not_7 (not_7_out, a1);
  and and_5 (and_5_out, not_7_out, not_8_out);
  not not_8 (not_8_out, a3);
  or or_1 (u1, and_1_out, and_2_out, and_3_out);
  and and_6 (and_6_out, not_1_out, a2, a3);
  or or_2 (u2, and_6_out, and_7_out);
  and and_7 (and_7_out, a1, not_2_out, not_3_out, not_4_out);
  or or_3 (u3, and_4_out, and_5_out);
endmodule

module counter_to_7segDisplay (
  input  a1,
  input  a2,
  input  a3,
  input  a4,
  output e,
  output d,
  output c,
  output b,
  output a,
  output f,
  output g
);

  wire and_1_out, and_2_out, and_3_out, and_4_out, and_5_out, and_6_out, and_7_out, and_8_out, and_9_out,
       and_10_out, and_11_out, and_12_out, and_13_out, and_14_out, and_15_out, and_16_out, and_17_out,
       and_18_out, and_19_out, and_20_out, and_21_out, and_22_out, and_23_out, and_24_out, and_25_out,
       and_26_out, and_27_out, and_28_out, and_29_out, not_1_out, not_2_out, not_3_out, not_4_out, not_5_out,
       not_6_out, not_7_out, not_8_out, not_9_out, not_10_out, not_11_out, not_12_out, not_13_out,
       not_14_out, not_15_out, not_16_out, not_17_out, not_18_out, not_19_out, not_20_out, not_21_out,
       not_22_out, not_23_out, not_24_out, not_25_out, not_26_out, not_27_out, not_28_out, not_29_out,
       not_30_out, not_31_out, not_32_out, not_33_out, not_34_out, not_35_out, not_36_out, not_37_out,
       not_38_out, not_39_out, not_40_out, not_41_out, not_42_out, not_43_out;

  not not_1 (not_1_out, a1);
  not not_2 (not_2_out, a3);
  not not_3 (not_3_out, a4);
  not not_4 (not_4_out, a1);
  not not_5 (not_5_out, a4);
  not not_6 (not_6_out, a1);
  not not_7 (not_7_out, a2);
  not not_8 (not_8_out, a3);
  not not_9 (not_9_out, a1);
  not not_10 (not_10_out, a1);
  not not_11 (not_11_out, a4);
  not not_12 (not_12_out, a2);
  not not_13 (not_13_out, a4);
  not not_14 (not_14_out, a3);
  not not_15 (not_15_out, a2);
  not not_16 (not_16_out, a3);
  and and_1 (and_1_out, not_16_out, a4);
  not not_17 (not_17_out, a1);
  and and_2 (and_2_out, not_17_out, a3, not_18_out);
  not not_18 (not_18_out, a4);
  and and_3 (and_3_out, a1, not_19_out);
  not not_19 (not_19_out, a3);
  and and_4 (and_4_out, a1, a4);
  not not_20 (not_20_out, a1);
  and and_5 (and_5_out, not_20_out, a3);
  and and_6 (and_6_out, a1, not_21_out);
  not not_21 (not_21_out, a3);
  not not_22 (not_22_out, a1);
  not not_23 (not_23_out, a3);
  and and_7 (and_7_out, not_22_out, not_23_out, not_24_out);
  not not_24 (not_24_out, a4);
  not not_25 (not_25_out, a2);
  and and_8 (and_8_out, not_25_out, a4);
  not not_26 (not_26_out, a1);
  and and_9 (and_9_out, not_26_out, a2, a3);
  not not_27 (not_27_out, a3);
  and and_10 (and_10_out, a1, not_27_out, a4);
  and and_11 (and_11_out, a1, a3, not_28_out);
  not not_28 (not_28_out, a4);
  not not_29 (not_29_out, a1);
  not not_30 (not_30_out, a2);
  not not_31 (not_31_out, a3);
  not not_32 (not_32_out, a1);
  not not_33 (not_33_out, a2);
  not not_34 (not_34_out, a4);
  not not_35 (not_35_out, a2);
  not not_36 (not_36_out, a3);
  not not_37 (not_37_out, a4);
  not not_38 (not_38_out, a1);
  and and_12 (and_12_out, not_38_out, not_39_out);
  not not_39 (not_39_out, a2);
  not not_40 (not_40_out, a1);
  and and_13 (and_13_out, not_40_out, a3);
  not not_41 (not_41_out, a2);
  and and_14 (and_14_out, not_41_out, a3);
  and and_15 (and_15_out, a2, not_42_out);
  not not_42 (not_42_out, a4);
  and and_16 (and_16_out, a1, a2, not_43_out);
  not not_43 (not_43_out, a3);
  and and_17 (and_17_out, not_1_out, not_2_out, not_3_out);
  and and_18 (and_18_out, not_4_out, a2, a3, a4);
  or or_1 (e, and_17_out, and_18_out, and_19_out);
  and and_19 (and_19_out, a1, a3, not_5_out);
  and and_20 (and_20_out, not_6_out, not_7_out, not_8_out);
  and and_21 (and_21_out, not_9_out, a3, a4);
  and and_22 (and_22_out, not_10_out, a2, not_11_out);
  and and_23 (and_23_out, a1, not_12_out, a3);
  and and_24 (and_24_out, a1, a3, not_13_out);
  and and_25 (and_25_out, a1, a2, not_14_out, a4);
  or or_2 (c, not_15_out, and_1_out, and_2_out, and_3_out, and_4_out);
  or or_3 (b, and_5_out, a2, and_6_out);
  or or_4 (a, and_7_out, and_8_out, and_9_out, and_10_out, and_11_out);
  and and_26 (and_26_out, not_29_out, not_30_out, not_31_out);
  and and_27 (and_27_out, not_32_out, not_33_out, not_34_out);
  and and_28 (and_28_out, a1, not_35_out, a3);
  and and_29 (and_29_out, a1, a2, not_36_out, not_37_out);
  or or_5 (g, and_12_out, and_13_out, and_14_out, and_15_out, and_16_out);
  or or_6 (d, and_20_out, and_21_out, and_22_out, and_23_out, and_24_out, and_25_out);
  or or_7 (f, and_26_out, and_27_out, and_28_out, and_29_out);
endmodule

module pedestrian_contr (
  input  a1,
  input  a2,
  input  a3,
  input  a4,
  output g,
  output r
);

  wire and_1_out, and_2_out, and_3_out, and_4_out, not_1_out, not_2_out, not_3_out, not_4_out;

  and and_1 (and_1_out, a1, a4);
  and and_2 (and_2_out, a1, a3);
  and and_3 (and_3_out, a1, a2);
  not not_1 (not_1_out, a1);
  not not_2 (not_2_out, a2);
  and and_4 (and_4_out, not_2_out, not_3_out, not_4_out);
  not not_3 (not_3_out, a3);
  not not_4 (not_4_out, a4);
  or or_1 (g, and_1_out, and_2_out, and_3_out);
  or or_2 (r, not_1_out, and_4_out);
endmodule
